// Logisim project labo_chenillard_etu.circ as structural Verilog: 5 circuits, main circuit MAXV_CHENILLARD
module MAXV_CHENILLARD (
  input  load_i,
  input  [7:0] switch_i,
  input  clk_i,
  input  nReset_i,
  output [7:0] led_o
);

  wire entree_i_sw7, entree_i_sw8, not_1_out;
  wire [1:0] entree_i_sw2;

  DipSwitch entree_i (
    .sw1(entree_i_sw2[1]), .sw2(entree_i_sw2[0]), .sw7(entree_i_sw7), .sw8(entree_i_sw8));  // open: sw3, sw4, sw5, sw6
  not not_1 (not_1_out, nReset_i);
  chenillard_TOP chenillard_top_1 (
    .load_i(load_i), .enable_i(entree_i_sw7), .right_nleft_i(entree_i_sw8), .speed_i(entree_i_sw2),
    .val_i(switch_i), .clk_i(clk_i), .reset_i(not_1_out), .led_o(led_o));

  // Notes on the sheet:
  //   Attention, votre version de Logisim
  //   ne contient pas de tracker. Si vous
  //   enregistrez votre projet, toutes les
  //   informations du tracker seront
  //   définitivement effacées.
endmodule

module chenillard_TOP (
  input  load_i,
  input  enable_i,
  input  right_nleft_i,
  input  [1:0] speed_i,
  input  [7:0] val_i,
  input  clk_i,
  input  reset_i,
  output [7:0] led_o
);


  // Notes on the sheet:
  //   Attention, votre version de Logisim
  //   ne contient pas de tracker. Si vous
  //   enregistrez votre projet, toutes les
  //   informations du tracker seront
  //   définitivement effacées.
endmodule

module shift_reg_4b (
  input  ser_r_i,
  input  ser_l_i,
  input  [3:0] value_load_i,
  input  [1:0] mode_i,
  input  clk_i,
  input  reset_i,
  output [3:0] val_o
);


  // Notes on the sheet:
  //   Attention, votre version de Logisim
  //   ne contient pas de tracker. Si vous
  //   enregistrez votre projet, toutes les
  //   informations du tracker seront
  //   définitivement effacées.
endmodule

module shift_reg_8b (
  input  ser_r_i,
  input  ser_l_i,
  input  [7:0] value_load_i,
  input  [1:0] mode_i,
  input  clk_i,
  input  reset_i,
  output [7:0] val_o
);


  // Notes on the sheet:
  //   Attention, votre version de Logisim
  //   ne contient pas de tracker. Si vous
  //   enregistrez votre projet, toutes les
  //   informations du tracker seront
  //   définitivement effacées.
endmodule

module timer_28b (
  input  [27:0] value_i,
  input  en_i,
  input  load_i,
  input  clk_i,
  input  reset_i,
  output done_o
);


  // Notes on the sheet:
  //   Attention, votre version de Logisim
  //   ne contient pas de tracker. Si vous
  //   enregistrez votre projet, toutes les
  //   informations du tracker seront
  //   définitivement effacées.
endmodule
